// Logisim project regfile.circ as structural Verilog: 1 circuit, main circuit regfile
module regfile (
  input  [4:0] rs1,
  input  [4:0] rs2,
  input  [4:0] rd,
  input  [31:0] Write_Data,
  input  RegWEn,
  input  clk,
  output [31:0] ra,
  output [31:0] sp,
  output [31:0] t0,
  output [31:0] t1,
  output [31:0] t2,
  output [31:0] s0,
  output [31:0] s1,
  output [31:0] a0,
  output [31:0] Read_Data_1,
  output [31:0] Read_Data_2
);

  wire [31:0] final_data, pre_data, ra_write, x0;

  Multiplexer #(.enable("false"), .select(5), .width(32)) multiplexer_1 (
    .in0(x0), .in1(ra), .out(Read_Data_1), .sel(rs1));  // open: in2, in3, in4, in5, in6, in7, in8, in9, in10, in11, in12, in13, in14, in15, in16, in17, in18, in19, in20, in21, in22, in23, in24, in25, in26, in27, in28, in29, in30, in31
  Multiplexer #(.enable("false"), .select(5), .width(32)) multiplexer_2 (
    .in0(x0), .out(Read_Data_2), .sel(rs2));  // open: in1, in2, in3, in4, in5, in6, in7, in8, in9, in10, in11, in12, in13, in14, in15, in16, in17, in18, in19, in20, in21, in22, in23, in24, in25, in26, in27, in28, in29, in30, in31
  Multiplexer #(.enable("false"), .select(5), .width(32)) multiplexer_3 (
    .in1(ra), .out(pre_data), .sel(rd));  // open: in0, in2, in3, in4, in5, in6, in7, in8, in9, in10, in11, in12, in13, in14, in15, in16, in17, in18, in19, in20, in21, in22, in23, in24, in25, in26, in27, in28, in29, in30, in31
  Demultiplexer #(.enable("false"), .select(5), .width(32)) demultiplexer_1 (
    .out1(ra_write), .in(final_data), .sel(rd));  // open: out0, out2, out3, out4, out5, out6, out7, out8, out9, out10, out11, out12, out13, out14, out15, out16, out17, out18, out19, out20, out21, out22, out23, out24, out25, out26, out27, out28, out29, out30, out31
  Multiplexer #(.enable("false"), .width(32)) multiplexer_4 (
    .in0(pre_data), .in1(Write_Data), .out(final_data), .sel(RegWEn));
  Register #(.width(32)) register_1 (.D({32{1'b0}}), .clk(clk), .Q(x0), .clr(1'b1));  // open: en
  Register register_2 (.clk(clk));  // open: D, en, Q, clr
  Register register_3 (.clk(clk));  // open: D, en, Q, clr
  Register #(.width(32)) register_4 (.D(ra_write), .clk(clk), .Q(ra));  // open: en, clr
  Register register_5 (.clk(clk));  // open: D, en, Q, clr
  Register register_6 (.clk(clk));  // open: D, en, Q, clr
  Register register_7 (.clk(clk));  // open: D, en, Q, clr
  Register register_8 (.clk(clk));  // open: D, en, Q, clr
  Register register_9 (.clk(clk));  // open: D, en, Q, clr

  // Other names for the same wires on the sheet: read_data1[31:0] = Read_Data_1; read_data2[31:0] = Read_Data_2;
  //   read_reg1[4:0] = rs1; read_reg2[4:0] = rs2; write_en = RegWEn; write_reg[4:0] = rd

  // Notes on the sheet:
  //   INPUTS to your circuit
  //   DON'T CHANGE THE LOCATIONS OF THE INPUTS AND OUTPUTS!
  //   These are DEBUG/TEST outputs from your circuit.
  //   OUTPUTS from your circuit
endmodule
